# Fritzing sketch ckt_diagram (saved by Fritzing 0.9.2b)
breadboards: 2

parts:
  Part1 = Bluetooth HC-05 Macho  # not connected
  TCRT9 = TCRT5000 sensor module [part_number=151608]  # not connected
  TCRT10 = TCRT5000 sensor module [part_number=151608]  # not connected
  TCRT11 = TCRT5000 sensor module [part_number=151608]  # not connected
  TCRT12 = TCRT5000 sensor module [part_number=151608]  # not connected
  TCRT13 = TCRT5000 sensor module [part_number=151608]  # not connected
  TCRT14 = TCRT5000 sensor module [part_number=151608]  # not connected
  TCRT15 = TCRT5000 sensor module [part_number=151608]  # not connected
  TCRT16 = TCRT5000 sensor module [part_number=151608]  # not connected
  Part2 = Arduino Nano (Rev3.0)  # not connected
  S1 = H-Bridge with L298N
  U1 = LIPO-110mAh [package=lipo-110]
  U2 = LIPO-110mAh [package=lipo-110]
  U3 = LIPO-110mAh [package=lipo-110]
  M2 = DC Motor
  M3 = DC Motor

nets:
  N1: S1.12V, U3.+
  N2: S1.GND, U1.-
  N3: S1.OUT4-Motor2, M2.pin_1
  N4: S1.OUT1-Motor1, M3.pin_1
  N5: S1.OUT2-Motor1, M3.pin_2
  N6: U1.+, U2.-
  N7: U2.+, U3.-

custom parts:
  TCRT5000 sensor module: breakout board with TCRT5000
  H-Bridge with L298N: h-bridge
